# Fritzing sketch can_cable (saved by Fritzing 1.0.4)
circuit board: 3.32129cm x 1.99008cm
breadboards: 1

parts:
  U1 = RJ45 Jack [package=rj45-8]
  J1 = female pin header, 2 pins [form="♀ (female)"]
  J2 = female pin header, 2 pins [form="♀ (female)"]

nets:
  N1: U1.1, J1.pin2
  N2: U1.2, J1.pin1
  N3: U1.3, U1.4, U1.5, J2.pin2
  N4: U1.6, U1.7, U1.8, J2.pin1
